# Fritzing sketch ControladorTemperatura (saved by Fritzing 0.7.10b)
breadboards: 1

parts:
  Arduino1 = Arduino
  Parte1 = Real Time Clock Module - DS1307 RTC Breakout Board
  LCD1 = LCD screen
  U1 = 74HC595 [package="DIP16 [THT]"]
  LED1 = Blue LED - 5mm [package="5 mm [THT]"]  # not connected
  LED3 = yellow LED - 5mm [package="5 mm [THT]"]  # not connected
  LED4 = LED - 5mm [color="Red (633nm)" package="5 mm [THT]"]  # not connected
  J1 = Piezo Speaker  # not connected
  R1 = Rotary Potentiometer (Large) [maximum_resistance=10kΩ package=THT]
  T2 = TMP36 Temperature Sensor [package="TO92 [THT]"]  # not connected

nets:
  N1: Arduino1.D4, LCD1.E, U1.ST_CP
  N2: Arduino1.D3, U1.DS
  N3: Arduino1.D2, Parte1.SQW
  N4: Arduino1.D1TX, U1.SH_CP, U1.VCC
  +5V: Arduino1.+5V, Parte1.5V, LCD1.VDD, LCD1.LED+, U1.MR, R1.leg1
  GND: Arduino1.GND, Parte1.GND, LCD1.VSS, LCD1.R/W, LCD1.LED-, U1.GND, U1.OE, R1.leg2
  N5: Arduino1.A4, Parte1.SDA
  N6: Arduino1.A5, Parte1.SCL
  N7: LCD1.V0, R1.wiper
  N8: LCD1.RS, U1.Q2
  N9: LCD1.DB4, U1.Q3
  N10: LCD1.DB5, U1.Q4
  N11: LCD1.DB6, U1.Q5
  N12: LCD1.DB7, U1.Q6

notes:
  #1: Clock del 595
  #2: DS del RTC
  #3: Data del 595
  #4: Enabled del 595
